# Fritzing sketch Lamp (saved by Fritzing 0.9.3b)

parts:
  Part1 = Ethernet Pro
  Part2 = Arduino Uno (Rev3) - ICSP  # not connected
  KY-1 = Keyes Relay [package=THT]
  LED1 = LEDs [package=led10mm]
  Power_plug1 = Power plug

nets:
  N1: Part1.IO6, KY-1.signal
  N2: Part1.5V, KY-1.power
  N3: Part1.GND, KY-1.ground
  N4: KY-1.NC, LED1.A
  N5: KY-1.C, Power_plug1.VCC
  N6: LED1.C, Power_plug1.GND

notes:
  Lamp
  Arduino uno R3 + Ethernetshield
  SDR-05VDC-SL-C
  Power plug

custom parts:
  Keyes Relay: The Keyes 5V relay module is suitable for SCM development, home appliance control. It uses a 5V~12V TIL control signal which can control DC / AC signal.
  LEDs: LEDs Standard schematic elements and footprints for 5mm, 3mm, 1206, and 0603 sized LEDs. 5mm - Spark Fun Electronics SKU : COM-00529 (and others)
