# Fritzing sketch Temp (saved by Fritzing 0.9.3b)
breadboards: 1

parts:
  Part1 = Arduino Uno (Rev3) - ICSP
  T1 = LM35 Temperature Sensor [package="TO92 [THT]"]
  R1 = Photocell (LDR) [package=THT]
  R2 = Resistor [tolerance=±20% resistance=1k package=THT]
  Part2 = Ethernet Pro  # not connected

nets:
  N1: Part1.A0, T1.Vout
  N2: Part1.A1, R1.pin_1, R2.Pin_0
  GND: Part1.GND, T1.GND, R2.Pin_1
  N3: Part1.5V, T1.+Vs, R1.pin_0

notes:
  LM35 (Tempratuur sensor)
  LDR (lichtsensor)
  1k resistor
  Arduino uno R3 + Ethernetshield
